// Logisim project Lab6.circ as structural Verilog: 1 circuit, main circuit main
module main (
  input  [1:0] Access_Mem,
  input  [31:0] Mem_Address,
  input  [31:0] Mem_Write,
  input  Mem_Write_Enable
);

  wire and_1_out, and_2_out, and_3_out, and_4_out, and_5_out, and_6_out, and_7_out, and_8_out, b_0, b_1, b_2,
       b_3, clock_1_out, is_byte, is_hw, is_w, not_1_out, not_2_out, not_3_out, not_4_out, not_5_out,
       not_6_out, not_7_out, not_8_out;
  wire [31:0] ram_1_dout;

  not not_1 (not_1_out, Mem_Address[1]);
  and and_1 (and_1_out, is_byte, not_1_out, not_3_out);
  not not_2 (not_2_out, Mem_Address[1]);
  not not_3 (not_3_out, Mem_Address[0]);
  and and_2 (and_2_out, not_2_out, is_hw);
  or r_0 (b_0, and_1_out, is_w, and_2_out);
  not not_4 (not_4_out, Mem_Address[1]);
  not not_5 (not_5_out, Mem_Address[1]);
  and and_3 (and_3_out, is_byte, not_4_out, Mem_Address[0]);
  and and_4 (and_4_out, not_5_out, is_hw);
  or r_1 (b_1, and_3_out, is_w, and_4_out);
  Clock clock_1 (.out(clock_1_out));
  not not_6 (not_6_out, Mem_Address[0]);
  and and_5 (and_5_out, is_byte, Mem_Address[1], not_6_out);
  and and_6 (and_6_out, Mem_Address[1], is_hw);
  or r_3 (b_2, and_5_out, is_w, and_6_out);
  and and_7 (and_7_out, is_byte, Mem_Address[1], Mem_Address[0]);
  and and_8 (and_8_out, is_hw, Mem_Address[1]);
  or r_4 (b_3, and_7_out, is_w, and_8_out);
  nor \byte  (is_byte, Access_Mem[0], Access_Mem[1]);
  not not_7 (not_7_out, Access_Mem[1]);
  and halfword (is_hw, Access_Mem[0], not_7_out);
  not not_8 (not_8_out, Access_Mem[0]);
  and word (is_w, not_8_out, Access_Mem[1]);
  RAM #(.addrWidth(24), .byteenables("byteEnables"), .dataWidth(32)) ram_1 (
    .addr(Mem_Address[31:8]), .we(Mem_Write_Enable), .oe(1'b1), .clk(clock_1_out), .din(Mem_Write),
    .dout(ram_1_dout), .be3(b_3), .be2(b_2), .be1(b_1), .be0(b_0));

  // Other names for the same wires on the sheet: addr_0_1[1:0] = Mem_Address[1:0]

  // Notes on the sheet:
  //   Byte Writing Logic
endmodule
